// Logisim project cpu.circ as structural Verilog: 1 circuit, main circuit main
module main (
);

  wire and_1_out, and_2_out, button_1_out, button_3_out, clk, counter_1_carry, d_ff_1_q, d_ff_2_q, d_ff_3_q,
       demultiplexer_1_out0, demultiplexer_1_out1, demultiplexer_1_out2, demultiplexer_1_out3,
       demultiplexer_1_out4, demultiplexer_1_out5, demultiplexer_1_out6, demultiplexer_1_out7,
       demultiplexer_1_out8, demultiplexer_1_out9, demultiplexer_1_out10, demultiplexer_1_out11,
       demultiplexer_1_out12, demultiplexer_1_out13, demultiplexer_1_out14, demultiplexer_1_out15,
       demultiplexer_2_out0, demultiplexer_2_out1, demultiplexer_2_out2, demultiplexer_2_out3,
       demultiplexer_2_out4, demultiplexer_2_out5, demultiplexer_2_out6, demultiplexer_2_out7,
       demultiplexer_2_out8, demultiplexer_2_out9, demultiplexer_2_out10, demultiplexer_2_out11,
       demultiplexer_2_out12, demultiplexer_2_out13, demultiplexer_2_out14, demultiplexer_2_out15, exec_op,
       i_ctrl, i_io, i_math, i_mem, i_reg, io_save, MC_DONE, MC_IO_READ_BUS_A, MC_IO_READ_BUS_B,
       MC_IO_WRITE_BUS_A, MC_IO_WRITE_BUS_B, MC_PUT_REG_IOP0_HI_BUS, MC_PUT_REG_IOP0_LO_BUS,
       MC_PUT_VAL_IOP0_BUS, MC_PUT_VAL_IOP1_BUS, MC_RAM_READ_BUS_A, MC_RAM_READ_BUS_B, MC_RAM_WRITE_BUS_A,
       MC_RAM_WRITE_BUS_B, MC_STR_REG_0_BUS, MC_STR_REG_1_BUS, MC_STR_REG_2_BUS, MC_STR_REG_3_BUS,
       MC_STR_REG_IOP0_HI_BUS, MC_STR_REG_IOP0_LO_BUS, op_done, or_1_out, or_2_out, or_20_out, or_38_out,
       or_40_out, or_42_out, ram_save, reg0w, reg1w, reg2w, reg3w, reg4w, reg5w, reg6w, reg7w, reg8w, reg9w,
       reg10w, reg11w, reg12w, reg13w, reg14w, reg15w, regwi1, regwi2, res, res_mc_counter, xor_1_out,
       xor_3_out, xor_4_out;
  wire [3:0] mc_counter, regs1, regs2, rom_1_data, rom_1_data_3, rom_1_data_4, rom_1_data_5, rom_1_data_6,
       rom_1_data_7, rom_1_data_8, rom_1_data_9;
  wire [3:3] not_1_out;
  wire [7:0] data_bus, demultiplexer_3_out0, demultiplexer_3_out1, demultiplexer_3_out2,
       demultiplexer_3_out3, demultiplexer_3_out4, demultiplexer_3_out5, demultiplexer_3_out6,
       demultiplexer_3_out7, demultiplexer_3_out8, demultiplexer_3_out9, demultiplexer_3_out10,
       demultiplexer_3_out11, demultiplexer_3_out12, demultiplexer_3_out13, demultiplexer_3_out14,
       demultiplexer_3_out15, demultiplexer_4_out0, demultiplexer_4_out1, demultiplexer_4_out2,
       demultiplexer_4_out3, demultiplexer_4_out4, demultiplexer_4_out5, demultiplexer_4_out6,
       demultiplexer_4_out7, demultiplexer_4_out8, demultiplexer_4_out9, demultiplexer_4_out10,
       demultiplexer_4_out11, demultiplexer_4_out12, demultiplexer_4_out13, demultiplexer_4_out14,
       demultiplexer_4_out15, io_in, io_out, iop, op0, op1, ram_in, ram_out, reg0d, reg0o, reg1d, reg1o,
       reg2d, reg2o, reg3d, reg3o, reg4d, reg4o, reg5d, reg5o, reg6d, reg6o, reg7d, reg7o, reg8d, reg8o,
       reg9d, reg9o, reg10d, reg10o, reg11d, reg11o, reg12d, reg12o, reg13d, reg13o, reg14d, reg14o, reg15d,
       reg15o, regdi1, regdi2, regdo1, regdo2;
  wire [15:0] counter_2_q, io_addr, ram_addr;
  wire [62:18] controlled_buffer_1_out;
  wire [63:32] rom_1_data_2;

  Demultiplexer #(.select(4)) demultiplexer_1 (
    .out0(demultiplexer_1_out0), .out1(demultiplexer_1_out1), .out2(demultiplexer_1_out2),
    .out3(demultiplexer_1_out3), .out4(demultiplexer_1_out4), .out5(demultiplexer_1_out5),
    .out6(demultiplexer_1_out6), .out7(demultiplexer_1_out7), .out8(demultiplexer_1_out8),
    .out9(demultiplexer_1_out9), .out10(demultiplexer_1_out10), .out11(demultiplexer_1_out11),
    .out12(demultiplexer_1_out12), .out13(demultiplexer_1_out13), .out14(demultiplexer_1_out14),
    .out15(demultiplexer_1_out15), .in(regwi1), .sel(regs1));
  Demultiplexer #(.select(4)) demultiplexer_2 (
    .out0(demultiplexer_2_out0), .out1(demultiplexer_2_out1), .out2(demultiplexer_2_out2),
    .out3(demultiplexer_2_out3), .out4(demultiplexer_2_out4), .out5(demultiplexer_2_out5),
    .out6(demultiplexer_2_out6), .out7(demultiplexer_2_out7), .out8(demultiplexer_2_out8),
    .out9(demultiplexer_2_out9), .out10(demultiplexer_2_out10), .out11(demultiplexer_2_out11),
    .out12(demultiplexer_2_out12), .out13(demultiplexer_2_out13), .out14(demultiplexer_2_out14),
    .out15(demultiplexer_2_out15), .in(regwi2), .sel(regs2));
  Counter #(.max('hf), .width(4)) counter_1 (
    .clr(or_1_out), .count(exec_op), .clk(clk), .carry(counter_1_carry), .Q(mc_counter));  // open: load, up, D
  or or_1 (or_1_out, res_mc_counter, res);
  ROM #(.addrWidth(12), .dataWidth(64)) rom_1 (
    .addr({iop, mc_counter}),
    .data({rom_1_data_2, rom_1_data, rom_1_data_3, rom_1_data_4, rom_1_data_5, rom_1_data_6, rom_1_data_7, rom_1_data_8, rom_1_data_9}));
  Pull_Resistor pull_resistor_1 (.node(regwi1));
  Pull_Resistor pull_resistor_2 (.node(regwi2));
  Pull_Resistor pull_resistor_3 (.node(regdi1));
  Pull_Resistor pull_resistor_4 (.node(regdi2));
  Pull_Resistor pull_resistor_5 (.node(regs1));
  Pull_Resistor pull_resistor_6 (.node(regs2));
  or or_2 (or_2_out, op_done, res);
  Button button_1 (.out(button_1_out));
  xor xor_1 (xor_1_out, button_1_out, clk);
  assign {MC_DONE, controlled_buffer_1_out, MC_IO_READ_BUS_B, MC_IO_READ_BUS_A, MC_IO_WRITE_BUS_B, MC_IO_WRITE_BUS_A, MC_RAM_READ_BUS_B, MC_RAM_READ_BUS_A, MC_RAM_WRITE_BUS_B, MC_RAM_WRITE_BUS_A, MC_STR_REG_3_BUS, MC_STR_REG_2_BUS, MC_STR_REG_1_BUS, MC_STR_REG_0_BUS, MC_PUT_VAL_IOP1_BUS, MC_PUT_VAL_IOP0_BUS, MC_STR_REG_IOP0_HI_BUS, MC_STR_REG_IOP0_LO_BUS, MC_PUT_REG_IOP0_HI_BUS, MC_PUT_REG_IOP0_LO_BUS} = and_1_out ? {rom_1_data_2, rom_1_data, rom_1_data_3, rom_1_data_4, rom_1_data_5, rom_1_data_6, rom_1_data_7, rom_1_data_8, rom_1_data_9} : 64'bz;  // Controlled_Buffer controlled_buffer_1
  Pull_Resistor pull_resistor_7 (.node(MC_PUT_REG_IOP0_LO_BUS));
  Pull_Resistor pull_resistor_8 (.node(MC_PUT_REG_IOP0_HI_BUS));
  Pull_Resistor pull_resistor_9 (.node(MC_STR_REG_IOP0_LO_BUS));
  Pull_Resistor pull_resistor_10 (.node(MC_STR_REG_IOP0_HI_BUS));
  Pull_Resistor pull_resistor_11 (.node(MC_PUT_VAL_IOP0_BUS));
  Pull_Resistor pull_resistor_12 (.node(MC_PUT_VAL_IOP1_BUS));
  Pull_Resistor pull_resistor_13 (.node(MC_STR_REG_0_BUS));
  Pull_Resistor pull_resistor_14 (.node(MC_STR_REG_1_BUS));
  Pull_Resistor pull_resistor_15 (.node(MC_STR_REG_2_BUS));
  Pull_Resistor pull_resistor_16 (.node(MC_STR_REG_3_BUS));
  Pull_Resistor pull_resistor_17 (.node(MC_RAM_WRITE_BUS_A));
  Pull_Resistor pull_resistor_18 (.node(MC_RAM_WRITE_BUS_B));
  Pull_Resistor pull_resistor_19 (.node(MC_RAM_READ_BUS_A));
  Pull_Resistor pull_resistor_20 (.node(MC_RAM_READ_BUS_B));
  Pull_Resistor pull_resistor_21 (.node(MC_IO_WRITE_BUS_A));
  Pull_Resistor pull_resistor_22 (.node(MC_IO_WRITE_BUS_B));
  Pull_Resistor pull_resistor_23 (.node(MC_IO_READ_BUS_A));
  Pull_Resistor pull_resistor_24 (.node(MC_IO_READ_BUS_B));
  Pull_Resistor pull_resistor_25 (.node(controlled_buffer_1_out[18]));
  Pull_Resistor pull_resistor_26 (.node(controlled_buffer_1_out[19]));
  Pull_Resistor pull_resistor_27 (.node(controlled_buffer_1_out[20]));
  Pull_Resistor pull_resistor_28 (.node(controlled_buffer_1_out[21]));
  Pull_Resistor pull_resistor_29 (.node(controlled_buffer_1_out[22]));
  Pull_Resistor pull_resistor_30 (.node(controlled_buffer_1_out[23]));
  Pull_Resistor pull_resistor_31 (.node(controlled_buffer_1_out[24]));
  Pull_Resistor pull_resistor_32 (.node(controlled_buffer_1_out[25]));
  Pull_Resistor pull_resistor_33 (.node(controlled_buffer_1_out[26]));
  Pull_Resistor pull_resistor_34 (.node(controlled_buffer_1_out[27]));
  Pull_Resistor pull_resistor_35 (.node(controlled_buffer_1_out[28]));
  Pull_Resistor pull_resistor_36 (.node(controlled_buffer_1_out[29]));
  Pull_Resistor pull_resistor_37 (.node(controlled_buffer_1_out[30]));
  Pull_Resistor pull_resistor_38 (.node(controlled_buffer_1_out[31]));
  Pull_Resistor pull_resistor_39 (.node(controlled_buffer_1_out[32]));
  Pull_Resistor pull_resistor_40 (.node(controlled_buffer_1_out[33]));
  Pull_Resistor pull_resistor_41 (.node(controlled_buffer_1_out[34]));
  Pull_Resistor pull_resistor_42 (.node(controlled_buffer_1_out[35]));
  Pull_Resistor pull_resistor_43 (.node(controlled_buffer_1_out[36]));
  Pull_Resistor pull_resistor_44 (.node(controlled_buffer_1_out[37]));
  Pull_Resistor pull_resistor_45 (.node(controlled_buffer_1_out[38]));
  Pull_Resistor pull_resistor_46 (.node(controlled_buffer_1_out[39]));
  Pull_Resistor pull_resistor_47 (.node(controlled_buffer_1_out[40]));
  Pull_Resistor pull_resistor_48 (.node(controlled_buffer_1_out[41]));
  Pull_Resistor pull_resistor_49 (.node(controlled_buffer_1_out[42]));
  Pull_Resistor pull_resistor_50 (.node(controlled_buffer_1_out[43]));
  Pull_Resistor pull_resistor_51 (.node(controlled_buffer_1_out[44]));
  Pull_Resistor pull_resistor_52 (.node(controlled_buffer_1_out[45]));
  Pull_Resistor pull_resistor_53 (.node(controlled_buffer_1_out[46]));
  Pull_Resistor pull_resistor_54 (.node(controlled_buffer_1_out[47]));
  Pull_Resistor pull_resistor_55 (.node(controlled_buffer_1_out[48]));
  Pull_Resistor pull_resistor_56 (.node(controlled_buffer_1_out[49]));
  Pull_Resistor pull_resistor_57 (.node(controlled_buffer_1_out[50]));
  Pull_Resistor pull_resistor_58 (.node(controlled_buffer_1_out[51]));
  Pull_Resistor pull_resistor_59 (.node(controlled_buffer_1_out[52]));
  Pull_Resistor pull_resistor_60 (.node(controlled_buffer_1_out[53]));
  Pull_Resistor pull_resistor_61 (.node(controlled_buffer_1_out[54]));
  Pull_Resistor pull_resistor_62 (.node(controlled_buffer_1_out[55]));
  Pull_Resistor pull_resistor_63 (.node(controlled_buffer_1_out[56]));
  Pull_Resistor pull_resistor_64 (.node(controlled_buffer_1_out[57]));
  Pull_Resistor pull_resistor_65 (.node(controlled_buffer_1_out[58]));
  Pull_Resistor pull_resistor_66 (.node(controlled_buffer_1_out[59]));
  Pull_Resistor pull_resistor_67 (.node(controlled_buffer_1_out[60]));
  Pull_Resistor pull_resistor_68 (.node(controlled_buffer_1_out[61]));
  Pull_Resistor pull_resistor_69 (.node(controlled_buffer_1_out[62]));
  Pull_Resistor pull_resistor_70 (.node(MC_DONE));
  or or_3 (reg0w, demultiplexer_1_out0, demultiplexer_2_out0);
  or or_4 (reg1w, demultiplexer_1_out1, demultiplexer_2_out1);
  or or_5 (reg2w, demultiplexer_1_out2, demultiplexer_2_out2);
  or or_6 (reg3w, demultiplexer_1_out3, demultiplexer_2_out3);
  or or_7 (reg4w, demultiplexer_1_out4, demultiplexer_2_out4);
  or or_8 (reg5w, demultiplexer_1_out5, demultiplexer_2_out5);
  or or_9 (reg6w, demultiplexer_1_out6, demultiplexer_2_out6);
  or or_10 (reg7w, demultiplexer_1_out7, demultiplexer_2_out7);
  or or_11 (reg8w, demultiplexer_1_out8, demultiplexer_2_out8);
  or or_12 (reg9w, demultiplexer_1_out9, demultiplexer_2_out9);
  or or_13 (reg10w, demultiplexer_1_out10, demultiplexer_2_out10);
  or or_14 (reg11w, demultiplexer_1_out11, demultiplexer_2_out11);
  or or_15 (reg12w, demultiplexer_1_out12, demultiplexer_2_out12);
  or or_16 (reg13w, demultiplexer_1_out13, demultiplexer_2_out13);
  or or_17 (reg14w, demultiplexer_1_out14, demultiplexer_2_out14);
  or or_18 (reg15w, demultiplexer_1_out15, demultiplexer_2_out15);
  D_Flip_Flop d_ff_1 (.D(1'b1), .clk(clk), .Q(d_ff_1_q), .reset(or_2_out));  // open: Qn, preset
  and and_1 (and_1_out, exec_op, clk);
  Demultiplexer #(.select(4), .width(8)) demultiplexer_3 (
    .out0(demultiplexer_3_out0), .out1(demultiplexer_3_out1), .out2(demultiplexer_3_out2),
    .out3(demultiplexer_3_out3), .out4(demultiplexer_3_out4), .out5(demultiplexer_3_out5),
    .out6(demultiplexer_3_out6), .out7(demultiplexer_3_out7), .out8(demultiplexer_3_out8),
    .out9(demultiplexer_3_out9), .out10(demultiplexer_3_out10), .out11(demultiplexer_3_out11),
    .out12(demultiplexer_3_out12), .out13(demultiplexer_3_out13), .out14(demultiplexer_3_out14),
    .out15(demultiplexer_3_out15), .in(regdi2), .sel(regs2));
  D_Flip_Flop d_ff_2 (.D(d_ff_1_q), .clk(clk), .Q(d_ff_2_q), .reset(or_2_out));  // open: Qn, preset
  xor xor_2 (res_mc_counter, d_ff_1_q, d_ff_2_q);
  Register #(.trigger("falling")) register_1 (.D(ram_out), .en(res_mc_counter), .clk(xor_1_out), .Q(iop), .clr(res));
  Pull_Resistor pull_resistor_71 (.node(clk));
  // Switch switch_1: pin names not known; wires that end beside it: 1'b1, clk
  Button button_2 (.out(res));
  Button button_3 (.out(button_3_out));
  and and_2 (and_2_out, and_1_out, MC_DONE);
  Hex_Digit_Display hex_digit_display_1 (.value(rom_1_data_2[63:60]));  // open: dp
  Demultiplexer #(.select(4), .width(8)) demultiplexer_4 (
    .out0(demultiplexer_4_out0), .out1(demultiplexer_4_out1), .out2(demultiplexer_4_out2),
    .out3(demultiplexer_4_out3), .out4(demultiplexer_4_out4), .out5(demultiplexer_4_out5),
    .out6(demultiplexer_4_out6), .out7(demultiplexer_4_out7), .out8(demultiplexer_4_out8),
    .out9(demultiplexer_4_out9), .out10(demultiplexer_4_out10), .out11(demultiplexer_4_out11),
    .out12(demultiplexer_4_out12), .out13(demultiplexer_4_out13), .out14(demultiplexer_4_out14),
    .out15(demultiplexer_4_out15), .in(regdi1), .sel(regs1));
  D_Flip_Flop d_ff_3 (.D(d_ff_2_q), .clk(clk), .Q(d_ff_3_q), .reset(or_2_out));  // open: Qn, preset
  xor xor_3 (xor_3_out, d_ff_2_q, d_ff_3_q);
  Register #(.trigger("falling")) register_2 (.D(ram_out), .en(xor_3_out), .clk(xor_1_out), .Q(op0), .clr(res));
  or or_19 (op_done, button_3_out, counter_1_carry, and_2_out);
  Hex_Digit_Display hex_digit_display_2 (.value(rom_1_data_2[59:56]));  // open: dp
  Hex_Digit_Display hex_digit_display_3 (.value(rom_1_data_2[55:52]));  // open: dp
  D_Flip_Flop d_ff_4 (.D(d_ff_3_q), .clk(clk), .Q(exec_op), .reset(or_2_out));  // open: Qn, preset
  xor xor_4 (xor_4_out, d_ff_3_q, exec_op);
  or or_20 (or_20_out, res_mc_counter, xor_3_out, xor_4_out);
  Register #(.trigger("falling")) register_3 (.D(ram_out), .en(xor_4_out), .clk(xor_1_out), .Q(op1), .clr(res));
  Hex_Digit_Display hex_digit_display_4 (.value(rom_1_data_2[51:48]));  // open: dp
  Hex_Digit_Display hex_digit_display_5 (.value(rom_1_data_2[47:44]));  // open: dp
  Hex_Digit_Display hex_digit_display_6 (.value(rom_1_data_2[43:40]));  // open: dp
  Hex_Digit_Display hex_digit_display_7 (.value(rom_1_data_2[39:36]));  // open: dp
  Counter #(.max('hffff), .width(16)) counter_2 (
    .clr(res), .count(or_20_out), .clk(clk), .Q(counter_2_q));  // open: load, up, D, carry
  Hex_Digit_Display hex_digit_display_8 (.value(rom_1_data));  // open: dp
  Hex_Digit_Display hex_digit_display_9 (.value(rom_1_data_2[35:32]));  // open: dp
  assign regs1 = MC_STR_REG_0_BUS ? 4'b0000 : 4'bz;  // Controlled_Buffer controlled_buffer_2
  assign regs1 = MC_STR_REG_1_BUS ? 4'b0001 : 4'bz;  // Controlled_Buffer controlled_buffer_3
  assign regs1 = MC_STR_REG_2_BUS ? 4'b0010 : 4'bz;  // Controlled_Buffer controlled_buffer_4
  assign regs1 = MC_STR_REG_3_BUS ? 4'b0011 : 4'bz;  // Controlled_Buffer controlled_buffer_5
  assign regs1 = MC_STR_REG_IOP0_LO_BUS ? op0[3:0] : 4'bz;  // Controlled_Buffer controlled_buffer_6
  assign regs1 = MC_STR_REG_IOP0_HI_BUS ? op0[7:4] : 4'bz;  // Controlled_Buffer controlled_buffer_7
  assign regs2 = MC_PUT_REG_IOP0_LO_BUS ? op0[3:0] : 4'bz;  // Controlled_Buffer controlled_buffer_8
  assign regs2 = MC_PUT_REG_IOP0_HI_BUS ? op0[7:4] : 4'bz;  // Controlled_Buffer controlled_buffer_9
  assign ram_addr = MC_RAM_WRITE_BUS_A ? {reg0o, reg1o} : 16'bz;  // Controlled_Buffer controlled_buffer_10
  assign ram_addr = MC_RAM_WRITE_BUS_B ? {reg0o, reg1o} : 16'bz;  // Controlled_Buffer controlled_buffer_11
  assign ram_addr = MC_RAM_READ_BUS_A ? {reg0o, reg1o} : 16'bz;  // Controlled_Buffer controlled_buffer_12
  assign ram_addr = MC_RAM_READ_BUS_B ? {reg0o, reg1o} : 16'bz;  // Controlled_Buffer controlled_buffer_13
  assign io_addr = MC_IO_WRITE_BUS_A ? {reg0o, reg1o} : 16'bz;  // Controlled_Buffer controlled_buffer_14
  assign io_addr = MC_IO_WRITE_BUS_B ? {reg0o, reg1o} : 16'bz;  // Controlled_Buffer controlled_buffer_15
  assign io_addr = MC_IO_READ_BUS_A ? {reg0o, reg1o} : 16'bz;  // Controlled_Buffer controlled_buffer_16
  assign io_addr = MC_IO_READ_BUS_B ? {reg0o, reg1o} : 16'bz;  // Controlled_Buffer controlled_buffer_17
  Hex_Digit_Display hex_digit_display_10 (.value(rom_1_data_3));  // open: dp
  Hex_Digit_Display hex_digit_display_11 (.value(rom_1_data_4));  // open: dp
  assign reg0d = demultiplexer_4_out0 | demultiplexer_3_out0;  // OR_Gate or_21, 8 bits wide
  assign reg1d = demultiplexer_4_out1 | demultiplexer_3_out1;  // OR_Gate or_22, 8 bits wide
  assign reg2d = demultiplexer_4_out2 | demultiplexer_3_out2;  // OR_Gate or_23, 8 bits wide
  assign reg3d = demultiplexer_4_out3 | demultiplexer_3_out3;  // OR_Gate or_24, 8 bits wide
  assign reg4d = demultiplexer_4_out4 | demultiplexer_3_out4;  // OR_Gate or_25, 8 bits wide
  assign reg5d = demultiplexer_4_out5 | demultiplexer_3_out5;  // OR_Gate or_26, 8 bits wide
  assign reg6d = demultiplexer_4_out6 | demultiplexer_3_out6;  // OR_Gate or_27, 8 bits wide
  assign reg7d = demultiplexer_4_out7 | demultiplexer_3_out7;  // OR_Gate or_28, 8 bits wide
  assign reg8d = demultiplexer_4_out8 | demultiplexer_3_out8;  // OR_Gate or_29, 8 bits wide
  assign reg9d = demultiplexer_4_out9 | demultiplexer_3_out9;  // OR_Gate or_30, 8 bits wide
  assign reg10d = demultiplexer_4_out10 | demultiplexer_3_out10;  // OR_Gate or_31, 8 bits wide
  assign reg11d = demultiplexer_4_out11 | demultiplexer_3_out11;  // OR_Gate or_32, 8 bits wide
  assign reg12d = demultiplexer_4_out12 | demultiplexer_3_out12;  // OR_Gate or_33, 8 bits wide
  assign reg13d = demultiplexer_4_out13 | demultiplexer_3_out13;  // OR_Gate or_34, 8 bits wide
  assign reg14d = demultiplexer_4_out14 | demultiplexer_3_out14;  // OR_Gate or_35, 8 bits wide
  assign reg15d = demultiplexer_4_out15 | demultiplexer_3_out15;  // OR_Gate or_36, 8 bits wide
  Hex_Digit_Display hex_digit_display_12 (.value(rom_1_data_5));  // open: dp
  Hex_Digit_Display hex_digit_display_13 (.value(rom_1_data_6));  // open: dp
  or or_37 (regwi1, MC_STR_REG_0_BUS, MC_STR_REG_1_BUS, MC_STR_REG_2_BUS, MC_STR_REG_3_BUS, MC_STR_REG_IOP0_LO_BUS, MC_STR_REG_IOP0_HI_BUS);
  or or_38 (or_38_out, MC_PUT_REG_IOP0_LO_BUS, MC_PUT_REG_IOP0_HI_BUS);
  or or_39 (ram_save, MC_RAM_WRITE_BUS_A, MC_RAM_WRITE_BUS_B);
  or or_40 (or_40_out, MC_RAM_READ_BUS_A, MC_RAM_READ_BUS_B);
  or or_41 (io_save, MC_IO_WRITE_BUS_A, MC_IO_WRITE_BUS_B);
  or or_42 (or_42_out, MC_IO_READ_BUS_A, MC_IO_READ_BUS_B);
  Multiplexer #(.select(4), .width(8)) multiplexer_1 (
    .in0(reg0o), .in1(reg1o), .in2(reg2o), .in3(reg3o), .in4(reg4o), .in5(reg5o), .in6(reg6o), .in7(reg7o),
    .in8(reg8o), .in9(reg9o), .in10(reg10o), .in11(reg11o), .in12(reg12o), .in13(reg13o), .in14(reg14o),
    .in15(reg15o), .out(regdo1), .sel(regs1));
  not not_1 (not_1_out[3], exec_op);
  assign ram_addr = or_20_out ? counter_2_q : 16'bz;  // Controlled_Buffer controlled_buffer_18
  Hex_Digit_Display hex_digit_display_14 (.value(rom_1_data_7));  // open: dp
  Hex_Digit_Display hex_digit_display_15 (.value(rom_1_data_8));  // open: dp
  Hex_Digit_Display hex_digit_display_16 (.value(op0[3:0]));  // open: dp
  assign data_bus = or_38_out ? regdo2 : 8'bz;  // Controlled_Buffer controlled_buffer_19
  assign ram_in = ram_save ? data_bus : 8'bz;  // Controlled_Buffer controlled_buffer_20
  assign data_bus = or_40_out ? ram_out : 8'bz;  // Controlled_Buffer controlled_buffer_21
  assign io_in = io_save ? data_bus : 8'bz;  // Controlled_Buffer controlled_buffer_22
  assign data_bus = or_42_out ? io_out : 8'bz;  // Controlled_Buffer controlled_buffer_23
  Demultiplexer #(.select(4)) demultiplexer_5 (
    .out0(i_reg), .out1(i_mem), .out2(i_io), .out3(i_math), .out4(i_ctrl), .in(1'b1),
    .sel({not_1_out[3], iop[6:4]}));  // open: out5, out6, out7, out8, out9, out10, out11, out12, out13, out14, out15
  Hex_Digit_Display hex_digit_display_17 (.value(rom_1_data_9));  // open: dp
  Multiplexer #(.select(4), .width(8)) multiplexer_2 (
    .in0(reg0o), .in1(reg1o), .in2(reg2o), .in3(reg3o), .in4(reg4o), .in5(reg5o), .in6(reg6o), .in7(reg7o),
    .in8(reg8o), .in9(reg9o), .in10(reg10o), .in11(reg11o), .in12(reg12o), .in13(reg13o), .in14(reg14o),
    .in15(reg15o), .out(regdo2), .sel(regs2));
  assign data_bus = MC_PUT_VAL_IOP0_BUS ? op0 : 8'bz;  // Controlled_Buffer controlled_buffer_24
  assign data_bus = MC_PUT_VAL_IOP1_BUS ? op1 : 8'bz;  // Controlled_Buffer controlled_buffer_25
  assign regdi1 = regwi1 ? data_bus : 8'bz;  // Controlled_Buffer controlled_buffer_26
  Hex_Digit_Display hex_digit_display_18 (.value(op0[7:4]));  // open: dp
  Hex_Digit_Display hex_digit_display_19 (.value(data_bus[7:4]));  // open: dp
  Hex_Digit_Display hex_digit_display_20 (.value(ram_addr[15:12]));  // open: dp
  Hex_Digit_Display hex_digit_display_21 (.value(ram_addr[11:8]));  // open: dp
  Hex_Digit_Display hex_digit_display_22 (.value(data_bus[3:0]));  // open: dp
  Pull_Resistor pull_resistor_72 (.node(data_bus));
  Hex_Digit_Display hex_digit_display_23 (.value(ram_addr[7:4]));  // open: dp
  Hex_Digit_Display hex_digit_display_24 (.value(ram_addr[3:0]));  // open: dp
  Hex_Digit_Display hex_digit_display_25 (.value(io_addr[15:12]));  // open: dp
  Hex_Digit_Display hex_digit_display_26 (.value(io_addr[11:8]));  // open: dp
  Hex_Digit_Display hex_digit_display_27 (.value(io_in[7:4]));  // open: dp
  Hex_Digit_Display hex_digit_display_28 (.value(io_in[3:0]));  // open: dp
  Register #(.trigger("falling")) register_4 (.D(reg0d), .en(reg0w), .clk(clk), .Q(reg0o), .clr(res));
  Hex_Digit_Display hex_digit_display_29 (.value(data_bus[7:4]));  // open: dp
  Hex_Digit_Display hex_digit_display_30 (.value(data_bus[3:0]));  // open: dp
  Pull_Resistor pull_resistor_73 (.node(data_bus));
  Hex_Digit_Display hex_digit_display_31 (.value(io_addr[7:4]));  // open: dp
  Hex_Digit_Display hex_digit_display_32 (.value(io_addr[3:0]));  // open: dp
  Hex_Digit_Display hex_digit_display_33 (.value(reg0o[7:4]));  // open: dp
  Hex_Digit_Display hex_digit_display_34 (.value(reg0o[3:0]));  // open: dp
  Hex_Digit_Display hex_digit_display_35 (.value(reg0o[7:4]));  // open: dp
  Hex_Digit_Display hex_digit_display_36 (.value(reg0o[3:0]));  // open: dp
  Hex_Digit_Display hex_digit_display_37 (.value(reg2o[7:4]));  // open: dp
  Hex_Digit_Display hex_digit_display_38 (.value(reg2o[3:0]));  // open: dp
  Hex_Digit_Display hex_digit_display_39 (.value(io_out[7:4]));  // open: dp
  Hex_Digit_Display hex_digit_display_40 (.value(reg1o[7:4]));  // open: dp
  Hex_Digit_Display hex_digit_display_41 (.value(reg1o[3:0]));  // open: dp
  Hex_Digit_Display hex_digit_display_42 (.value(reg3o[7:4]));  // open: dp
  Hex_Digit_Display hex_digit_display_43 (.value(reg3o[3:0]));  // open: dp
  Hex_Digit_Display hex_digit_display_44 (.value(ram_in[7:4]));  // open: dp
  Hex_Digit_Display hex_digit_display_45 (.value(ram_in[3:0]));  // open: dp
  Pull_Resistor pull_resistor_74 (.node(ram_in));
  Hex_Digit_Display hex_digit_display_46 (.value(ram_out[7:4]));  // open: dp
  Hex_Digit_Display hex_digit_display_47 (.value(ram_out[3:0]));  // open: dp
  Hex_Digit_Display hex_digit_display_48 (.value(io_out[3:0]));  // open: dp
  Register #(.trigger("falling")) register_5 (.D(reg1d), .en(reg1w), .clk(clk), .Q(reg1o), .clr(res));
  Hex_Digit_Display hex_digit_display_49 (.value(reg1o[7:4]));  // open: dp
  Hex_Digit_Display hex_digit_display_50 (.value(reg1o[3:0]));  // open: dp
  Pull_Resistor pull_resistor_75 (.node(ram_out));
  Register #(.trigger("falling")) register_6 (.D(reg2d), .en(reg2w), .clk(clk), .Q(reg2o), .clr(res));
  Hex_Digit_Display hex_digit_display_51 (.value(reg2o[7:4]));  // open: dp
  Hex_Digit_Display hex_digit_display_52 (.value(reg2o[3:0]));  // open: dp
  Register #(.trigger("falling")) register_7 (.D(reg3d), .en(reg3w), .clk(clk), .Q(reg3o), .clr(res));
  Hex_Digit_Display hex_digit_display_53 (.value(reg3o[7:4]));  // open: dp
  Hex_Digit_Display hex_digit_display_54 (.value(reg3o[3:0]));  // open: dp
  Register #(.trigger("falling")) register_8 (.D(reg4d), .en(reg4w), .clk(clk), .Q(reg4o), .clr(res));
  Hex_Digit_Display hex_digit_display_55 (.value(reg4o[7:4]));  // open: dp
  RAM #(.addrWidth(16), .enables("line"), .trigger("falling")) ram_1 (
    .addr(ram_addr), .we(ram_save), .oe(clk), .clk(clk), .din(ram_in), .dout(ram_out));
  Hex_Digit_Display hex_digit_display_56 (.value(reg4o[3:0]));  // open: dp
  Register #(.trigger("falling")) register_9 (.D(reg5d), .en(reg5w), .clk(clk), .Q(reg5o), .clr(res));
  Hex_Digit_Display hex_digit_display_57 (.value(reg5o[7:4]));  // open: dp
  Hex_Digit_Display hex_digit_display_58 (.value(reg5o[3:0]));  // open: dp
  Register #(.trigger("falling")) register_10 (.D(reg6d), .en(reg6w), .clk(clk), .Q(reg6o), .clr(res));
  Hex_Digit_Display hex_digit_display_59 (.value(reg6o[7:4]));  // open: dp
  Hex_Digit_Display hex_digit_display_60 (.value(reg6o[3:0]));  // open: dp
  Register #(.trigger("falling")) register_11 (.D(reg7d), .en(reg7w), .clk(clk), .Q(reg7o), .clr(res));
  Hex_Digit_Display hex_digit_display_61 (.value(reg7o[7:4]));  // open: dp
  Hex_Digit_Display hex_digit_display_62 (.value(reg7o[3:0]));  // open: dp
  Pull_Resistor pull_resistor_76 (.node(ram_in));
  Pull_Resistor pull_resistor_77 (.node(ram_save));
  Pull_Resistor pull_resistor_78 (.node(ram_addr));
  Pull_Resistor pull_resistor_79 (.node(ram_out));
  Register #(.trigger("falling")) register_12 (.D(reg8d), .en(reg8w), .clk(clk), .Q(reg8o), .clr(res));
  Hex_Digit_Display hex_digit_display_63 (.value(reg8o[7:4]));  // open: dp
  Hex_Digit_Display hex_digit_display_64 (.value(reg8o[3:0]));  // open: dp
  assign io_out = io_addr[15] ? 8'hab : 8'bz;  // Controlled_Buffer controlled_buffer_27
  Register #(.trigger("falling")) register_13 (.D(reg9d), .en(reg9w), .clk(clk), .Q(reg9o), .clr(res));
  Hex_Digit_Display hex_digit_display_65 (.value(reg9o[7:4]));  // open: dp
  Hex_Digit_Display hex_digit_display_66 (.value(reg9o[3:0]));  // open: dp
  Register #(.trigger("falling")) register_14 (.D(reg10d), .en(reg10w), .clk(clk), .Q(reg10o), .clr(res));
  Hex_Digit_Display hex_digit_display_67 (.value(reg10o[7:4]));  // open: dp
  Hex_Digit_Display hex_digit_display_68 (.value(reg10o[3:0]));  // open: dp
  Pull_Resistor pull_resistor_80 (.node(io_addr));
  Pull_Resistor pull_resistor_81 (.node(io_in));
  Pull_Resistor pull_resistor_82 (.node(io_out));
  Pull_Resistor pull_resistor_83 (.node(io_save));
  Register #(.trigger("falling")) register_15 (.D(reg11d), .en(reg11w), .clk(clk), .Q(reg11o), .clr(res));
  Hex_Digit_Display hex_digit_display_69 (.value(reg11o[7:4]));  // open: dp
  Hex_Digit_Display hex_digit_display_70 (.value(reg11o[3:0]));  // open: dp
  Hex_Digit_Display hex_digit_display_71 (.value(io_addr[15:12]));  // open: dp
  Hex_Digit_Display hex_digit_display_72 (.value(io_addr[11:8]));  // open: dp
  Hex_Digit_Display hex_digit_display_73 (.value(io_in[7:4]));  // open: dp
  Hex_Digit_Display hex_digit_display_74 (.value(io_in[3:0]));  // open: dp
  Hex_Digit_Display hex_digit_display_75 (.value(reg12o[7:4]));  // open: dp
  Hex_Digit_Display hex_digit_display_76 (.value(io_addr[7:4]));  // open: dp
  Hex_Digit_Display hex_digit_display_77 (.value(io_addr[3:0]));  // open: dp
  Register #(.trigger("falling")) register_16 (.D(reg12d), .en(reg12w), .clk(clk), .Q(reg12o), .clr(res));
  Hex_Digit_Display hex_digit_display_78 (.value(reg12o[3:0]));  // open: dp
  Hex_Digit_Display hex_digit_display_79 (.value(io_out[7:4]));  // open: dp
  Hex_Digit_Display hex_digit_display_80 (.value(io_out[3:0]));  // open: dp
  Register #(.trigger("falling")) register_17 (.D(reg13d), .en(reg13w), .clk(clk), .Q(reg13o), .clr(res));
  Hex_Digit_Display hex_digit_display_81 (.value(reg13o[7:4]));  // open: dp
  Hex_Digit_Display hex_digit_display_82 (.value(reg13o[3:0]));  // open: dp
  Register #(.trigger("falling")) register_18 (.D(reg14d), .en(reg14w), .clk(clk), .Q(reg14o), .clr(res));
  Hex_Digit_Display hex_digit_display_83 (.value(reg14o[7:4]));  // open: dp
  Hex_Digit_Display hex_digit_display_84 (.value(reg14o[3:0]));  // open: dp
  Hex_Digit_Display hex_digit_display_85 (.value(reg15o[7:4]));  // open: dp
  Register #(.trigger("falling")) register_19 (.D(reg15d), .en(reg15w), .clk(clk), .Q(reg15o), .clr(res));
  Hex_Digit_Display hex_digit_display_86 (.value(reg15o[3:0]));  // open: dp

  // Other names for the same wires on the sheet: iopsub[3:0] = iop[3:0]; op0subhigh[3:0] = op0[7:4];
  //   op0sublow[3:0] = op0[3:0]; regao[15:0] = {reg0o, reg1o}; regbo[15:0] = {reg2o, reg3o}

  // Notes on the sheet:
  //   contents of rom_1 (hex, n*v repeats v):
  //   9 8000000000000000 14*0 28 8000000000000000 14*0 50 a0 8000000000000000 13*0 110 220
  //   8000000000000000 13*0 8000000000000000 15*0 8000000000000000 15*0 8000000000000000 15*0
  //   8000000000000000 15*0 8000000000000000 15*0 8000000000000000 15*0 8000000000000000 15*0
  //   8000000000000000 15*0 8000000000000000 15*0 8000000000000000 15*0 8000000000000000 15*0
  //   8000000000000000 15*0 1008 8000000000000000 14*0 2008 8000000000000000 14*0 402 8000000000000000
  //   14*0 802 8000000000000000 14*0 8000000000000000 15*0 8000000000000000 15*0 8000000000000000 15*0
  //   8000000000000000 15*0 8000000000000000 15*0 8000000000000000 15*0 8000000000000000 15*0
  //   8000000000000000 15*0 8000000000000000 15*0 8000000000000000 15*0 8000000000000000 15*0
  //   8000000000000000 15*0 10008 8000000000000000 14*0 20008 8000000000000000 14*0 4002 8000000000000000
  //   14*0 8002 8000000000000000 14*0 8000000000000000 15*0 8000000000000000 15*0 8000000000000000 15*0
  //   8000000000000000 15*0 8000000000000000 15*0 8000000000000000 15*0 8000000000000000 15*0
  //   8000000000000000 15*0 8000000000000000 15*0 8000000000000000 15*0 8000000000000000 15*0
  //   8000000000000000 15*0 8000000000000000 15*0 8000000000000000 15*0 8000000000000000 15*0
  //   8000000000000000 15*0 8000000000000000 15*0 8000000000000000 15*0 8000000000000000 15*0
  //   8000000000000000 15*0 8000000000000000 15*0 8000000000000000 15*0 8000000000000000 15*0
  //   8000000000000000 15*0 8000000000000000 15*0 8000000000000000 15*0 8000000000000000 15*0
  //   8000000000000000 15*0 8000000000000000 15*0 8000000000000000 15*0 8000000000000000 15*0
  //   8000000000000000 15*0 8000000000000000 15*0 8000000000000000 15*0 8000000000000000 15*0
  //   8000000000000000 15*0 8000000000000000 15*0 8000000000000000 15*0 8000000000000000 15*0
  //   8000000000000000 15*0 8000000000000000 15*0 8000000000000000 15*0 8000000000000000 15*0
  //   8000000000000000 15*0 8000000000000000 15*0 8000000000000000 15*0 8000000000000000 15*0
  //   8000000000000000 15*0 8000000000000000 15*0 8000000000000000 15*0 8000000000000000 15*0
  //   8000000000000000 15*0 8000000000000000 15*0 8000000000000000 15*0 8000000000000000 15*0
  //   8000000000000000 15*0 8000000000000000 15*0 8000000000000000 15*0 8000000000000000 15*0
  //   8000000000000000 15*0 8000000000000000 15*0 8000000000000000 15*0 8000000000000000 15*0
  //   8000000000000000 15*0 8000000000000000 15*0 8000000000000000 15*0 8000000000000000 15*0
  //   8000000000000000 15*0 8000000000000000 15*0 8000000000000000 15*0 8000000000000000 15*0
  //   8000000000000000 15*0 8000000000000000 15*0 8000000000000000 15*0 8000000000000000 15*0
  //   8000000000000000 15*0 8000000000000000 15*0 8000000000000000 15*0 8000000000000000 15*0
  //   8000000000000000 15*0 8000000000000000 15*0 8000000000000000 15*0 8000000000000000 15*0
  //   8000000000000000 15*0 8000000000000000 15*0 8000000000000000 15*0 8000000000000000 15*0
  //   8000000000000000 15*0 8000000000000000 15*0 8000000000000000 15*0 8000000000000000 15*0
  //   8000000000000000 15*0 8000000000000000 15*0 8000000000000000 15*0 8000000000000000 15*0
  //   8000000000000000 15*0 8000000000000000 15*0 8000000000000000 15*0 8000000000000000 15*0
  //   8000000000000000 15*0 8000000000000000 15*0 8000000000000000 15*0 8000000000000000 15*0
  //   8000000000000000 15*0 8000000000000000 15*0 8000000000000000 15*0 8000000000000000 15*0
  //   8000000000000000 15*0 8000000000000000 15*0 8000000000000000 15*0 8000000000000000 15*0
  //   8000000000000000 15*0 8000000000000000 15*0 8000000000000000 15*0 8000000000000000 15*0
  //   8000000000000000 15*0 8000000000000000 15*0 8000000000000000 15*0 8000000000000000 15*0
  //   8000000000000000 15*0 8000000000000000 15*0 8000000000000000 15*0 8000000000000000 15*0
  //   8000000000000000 15*0 8000000000000000 15*0 8000000000000000 15*0 8000000000000000 15*0
  //   8000000000000000 15*0 8000000000000000 15*0 8000000000000000 15*0 8000000000000000 15*0
  //   8000000000000000 15*0 8000000000000000 15*0 8000000000000000 15*0 8000000000000000 15*0
  //   8000000000000000 15*0 8000000000000000 15*0 8000000000000000 15*0 8000000000000000 15*0
  //   8000000000000000 15*0 8000000000000000 15*0 8000000000000000 15*0 8000000000000000 15*0 800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
  //   REGISTER INPUT COMBINERS
  //   MICROCODE COUNTER
  //   MICROCODE ROM
  //   REGISTER MUXERS AND DEMUXERS
  //   CLOCK + RESET
  //   INSTRUCTION CYCLE + INSTRUCTION LOAD
  //   REGISTER COMBINATORS
  //   MICROCODE STEP
  //   INSTRUCTION SPLITTERS
  //   INSTRUCTION COUNTER
  //   INSTRUCTION SELECTOR
  //   DATA BUS
  //   RAM ADDR
  //   DATA BUS
  //   REGISTERS
  //   RAM IN
  //   RAM OUT
  //   RAM
  //   RAM CONTROLS
  //   TEST IO
  //   IO CONNECTION
endmodule
